# Fritzing sketch Schematic (saved by Fritzing 0.9.2b)
breadboards: 1

parts:
  Part1 = Arduino Uno (Rev3)
  Q1 = TIP120 Hi-Current Darlington Transistor
  R1 = Resistor [tolerance=±5% resistance=1k package="0603 [SMD]"]
  R2 = Resistor [tolerance=±5% resistance=1k package="0603 [SMD]"]
  Part2 = ST2012 2.8W Class D Stereo Amplifier
  SP1 = SPEAKER [package=pcb_mount_speaker]
  R3 = Resistor [tolerance=±5% resistance=1k package="0603 [SMD]"]
  R4 = Resistor [tolerance=±5% resistance=1k package="0603 [SMD]"]

nets:
  N1: Part1.D13/SCK, R1.Pin_0
  N2: Part1.D2, R4.Pin_0
  N3: Part1.D3_PWM, R4.Pin_1
  N4: Part1.D4, R3.Pin_0
  N5: Part1.D5_PWM, R3.Pin_1
  N6: Part1.D6_PWM, R2.Pin_0
  N7: Part1.D7, R2.Pin_1
  N8: Q1.BASE, R1.Pin_1
  N9: Q1.COLLECTOR, Part2.G0
  N10: Part2.R-, Part2.L-
  N11: Part2.RIGHT+, SP1.+
  N12: Part2.RIGHT-, SP1.-

notes:
  wire two (no polarity)
  wire one (no polarity)
  stereo bare wire
  capsense 3
  capsense 2
  capsense 1
  Not pictured:
  Seeed GPRS shield
  Adafruit battery shieldss
